# Fritzing sketch Gemma-earrings-kytkentä (saved by Fritzing 0.8.5b)

parts:
  Adafruit_Neopixel_ring_16 = Neopixel Ring 16
  pgm_change_btn = Pushbutton [package="[SMD]"]
  power_switch = Toggle Switch [package=THT]
  charge_connector = Header 2 [package=jst-2-smd]
  Adafruit_Gemma = Adafruit GEMMA
  150mAh_LiPo_battery = LIPO-150mAh [package=lipo-150]
  Adafruit_Micro_Lipo_charger = Adafruit microlipo USB charger [package=lipo-150]

nets:
  GND: Adafruit_Neopixel_ring_16.GND, Adafruit_Gemma.GND
  N1: Adafruit_Neopixel_ring_16.VCC, Adafruit_Gemma.Vout
  N2: Adafruit_Neopixel_ring_16.IN, Adafruit_Gemma.D1
  N3: pgm_change_btn.Pin_1, pgm_change_btn.Pin_2, Adafruit_Gemma.D0
  N4: pgm_change_btn.Pin_3, pgm_change_btn.Pin_4, Adafruit_Gemma.3Vo
  N5: power_switch.L1, charge_connector.1-in, 150mAh_LiPo_battery.+
  N6: power_switch.COM, Adafruit_Gemma.Battery_+
  N7: charge_connector.2-in, Adafruit_Gemma.Battery_-, 150mAh_LiPo_battery.-
  N8: charge_connector.2-out, Adafruit_Micro_Lipo_charger.-
  N9: charge_connector.1-out, Adafruit_Micro_Lipo_charger.+

custom parts:
  Neopixel Ring 16: Neopixel Ring x16
  Header 2: Header 2 Standard 2-pin 0.1 header. Use with straight break away headers (SKU : PRT-00116), right angle break away headers (PRT-00553), swiss pins (PRT-00743), machine pins (PRT-00117), and female headers (PRT-00115). Molex polarized connector foot print use with SKU : PRT-08233 with associated crimp pins and housings.
  Adafruit GEMMA: Adafruit Gemma wearable electronics main board. Edited to include jst connector attachment points
  LIPO-150mAh: 150mAh Lipo-battery
